# Fritzing sketch Hamster (saved by Fritzing 0.9.2b)
circuit board: 6.88566cm x 5.36311cm
breadboards: 1

parts:
  Part1 = Arduino Uno (Rev3)
  U1 = DRV8833
  Part2 = SRF05 Ultrasonic Rangefinder
  Part3 = Bluetooth HC-06
  VCC1 = 4 x AAA Battery Mount
  BREAKOUT1 = HMC5883L Compass Breakout
  Motor_-_Right = DC Motor  # not connected
  Motor_-_Left = DC Motor  # not connected
  LED1 = RGB LED - (4 legs) [package="5 mm [THT]"]
  R1 = Resistor [tolerance=±5% resistance=220 package="2010 [SMD]"]
  R2 = Resistor [tolerance=±5% resistance=220 package="2010 [SMD]"]
  LED2 = smd LED [color="Blue (430nm)" package="0603 [SMD]"]
  R4 = Resistor [tolerance=±5% resistance=220 package="2010 [SMD]"]
  R3 = Resistor [tolerance=±5% resistance=220 package="2010 [SMD]"]
  U3 = SWITCH_SPDT [package=kps-1290]
  R5 = Resistor [tolerance=±5% resistance=10k package=THT]
  R6 = Resistor [tolerance=±5% resistance=10k package=THT]

nets (from the breadboard view):
  N1: Part1.A2, Part3.RXD
  N2: Part1.A3, Part3.TXD
  N3: Part1.A4/SDA, BREAKOUT1.SDA
  N4: Part1.A5/SCL, BREAKOUT1.SCL
  N5: Part1.D8, U3.O, R5.Pin_1
  N6: Part1.D9_PWM, LED2.cathode, R4.Pin_0, R4.Pin_1
  N7: Part1.D10_PWM/SS, U1.AIN2
  N8: Part1.D11_PWM/MOSI, U1.AIN1
  N9: Part1.D12/MISO, Part2.Trig
  N10: Part1.D13/SCK, Part2.Echo
  N11: Part1.D2, LED1.green_cathode, R2.Pin_0, R2.Pin_1
  N12: Part1.D3_PWM, LED1.blue_cathode, R3.Pin_0, R3.Pin_1
  N13: Part1.D4, LED1.red_cathode, R1.Pin_0, R1.Pin_1
  N14: Part1.D5_PWM, U1.BIN1
  N15: Part1.D6_PWM, U1.BIN2
  N16: Part1.D7, U3.S, R6.Pin_1
  3V3: Part1.3V3, Part3.VCC
  N17: Part1.5V, U3.P
  GND: Part1.GND, U1.GND#0, Part2.GND, Part3.GND, VCC1.-, BREAKOUT1.GND, LED1.common_anode, LED2.anode, R5.Pin_0, R6.Pin_0
  N18: U1.VIN, VCC1.+

custom parts:
  DRV8833: The DRV8833 provides a dual bridge motor driver solution for toys, printers, and other mechatronic applications.
