# Fritzing sketch Schematic - Hamster 0.1.2 (saved by Fritzing 0.9.2b)
breadboards: 1

parts:
  Part1 = Arduino Uno (Rev3)
  Motor_-_Right = DC Motor
  VCC1 = 4 x AAA Battery Mount
  U1 = DRV8833
  Part2 = SRF05 Ultrasonic Rangefinder
  Motor_-_Left = DC Motor

nets:
  N1: Part1.D10_PWM/SS, U1.AIN2
  N2: Part1.D11_PWM/MOSI, U1.AIN1
  N3: Part1.D12/MISO, Part2.Trig
  N4: Part1.D13/SCK, Part2.Echo
  GND: Part1.GND, VCC1.-, U1.GND#0, Part2.GND
  N5: Part1.D5_PWM, U1.BIN1
  N6: Part1.D6_PWM, U1.BIN2
  5V: Part1.5V, Part2.VCC
  N7: Part1.VIN, VCC1.+
  N8: Motor_-_Right.pin_1, U1.AOUT2
  N9: Motor_-_Right.pin_2, U1.AOUT1
  N10: U1.BOUT1, Motor_-_Left.pin_2
  N11: U1.BOUT2, Motor_-_Left.pin_1

custom parts:
  DRV8833: The DRV8833 provides a dual bridge motor driver solution for toys, printers, and other mechatronic applications.
